# Fritzing sketch RobotWebControllerCircuit (saved by Fritzing 1.0.2b)
breadboards: 1

parts:
  A1 = u-blox NEO-6M GPS Breakout
  Part1 = Adafruit AirLift Breakout [part_number="Adafruit #4201"]
  Part2 = Arduino Mega 2560 (Rev3)

nets:
  N1: A1.Pin_1, Part1.VIN
  N2: A1.Pin_2, Part1.GND
  N3: A1.Pin_3, Part2.D18/TX1
  N4: A1.Pin_4, Part2.D19/RX1
  N5: Part1.CS, Part2.D10_PWM
  N6: Part1.ESP_BUSY, Part2.D9_PWM
  N7: Part1.RESET, Part2.D6_PWM

custom parts:
  Adafruit AirLift Breakout: Give your plain ol' microcontroller project a lift with the Adafruit AirLift - a breakout board that lets you use the powerful ESP32 as a WiFi co-processor. You probably have your favorite microcontroller (like the ATmega328 or ATSAMD51), awesome peripherals and lots of libraries. But it doesn't have WiFi built in! So lets give that chip a best friend, the ESP32. This chip can handle all the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
